# Fritzing sketch laser-sensor (saved by Fritzing 0.9.6b)
breadboards: 1

parts:
  P1 = S1133 Si Photodiode [package="8mm Ceramic [THT]"]
  D1 = Diode [package=diode-hv]
  D2 = Diode [package=diode-hv]
  P2 = S1133 Si Photodiode [package="8mm Ceramic [THT]"]
  R1 = Resistor [tolerance=±5% resistance=10k package="1206 [SMD]"]
  WeMos_D1_Mini1 = WeMos D1 Mini

nets:
  N1: P1.cathode, D1.A
  N2: P1.anode, WeMos_D1_Mini1.D7
  N3: D1.C, D2.C, R1.Pin_0, WeMos_D1_Mini1.A0
  N4: D2.A, P2.cathode
  N5: P2.anode, WeMos_D1_Mini1.D6
  N6: R1.Pin_1, WeMos_D1_Mini1.G
